// Logisim project machine.circ as structural Verilog
module CPU (
  input  [31:0] RAM_In,
  input  [15:0] ROM_In,
  input  Clk,
  input  Reset,
  output [7:0] ROM_Addr,
  output [31:0] R0,
  output [31:0] R4,
  output [31:0] RAM_Addr,
  output [31:0] R1,
  output [31:0] R5,
  output [31:0] RAM_Out,
  output Store,
  output [31:0] R2,
  output [31:0] R6,
  output [31:0] R3,
  output [31:0] R7
);

  wire ALU_p1, ALU_p2, banc_de_registre_1_p9, CONTROLLER_p2, CONTROLLER_p5, CONTROLLER_p8, CONTROLLER_p9;
  wire [4:0] bitselector_1_out, CONTROLLER_p7, multiplexer_2_out;
  wire [31:0] ALU_p8, CONTROLLER_p6, multiplexer_1_out, multiplexer_3_out;

  Multiplexer #(.width(32), .enable("false")) multiplexer_1 (
    .in0(ALU_p8), .in1(RAM_In), .out(multiplexer_1_out), .sel(CONTROLLER_p5));
  // CONTROLLER CONTROLLER: pin names not known; wires that end beside it: ROM_In, CONTROLLER_p2, Clk, Reset, CONTROLLER_p5, CONTROLLER_p6, CONTROLLER_p7, CONTROLLER_p8, CONTROLLER_p9
  // BANC_DE_REGISTRE banc_de_registre_1: pin names not known; wires that end beside it: multiplexer_1_out, R0, Clk, R1, Reset, R2, R3, R4, banc_de_registre_1_p9, R5, R6, R7
  BitSelector #(.width(32), .group(5)) bitselector_1 (.in(RAM_Out), .out(bitselector_1_out), .sel(3'b000));
  Multiplexer #(.width(5), .enable("false")) multiplexer_2 (
    .in0(bitselector_1_out), .in1(CONTROLLER_p7), .out(multiplexer_2_out), .sel(CONTROLLER_p8));
  Multiplexer #(.width(32), .enable("false")) multiplexer_3 (
    .in0(CONTROLLER_p6), .in1(RAM_Out), .out(multiplexer_3_out), .sel(banc_de_registre_1_p9));
  // ALU ALU: pin names not known; wires that end beside it: ALU_p1, ALU_p2, multiplexer_3_out, ALU_p2, multiplexer_2_out, CONTROLLER_p9, ALU_p1, ALU_p8, CONTROLLER_p2, Store
endmodule
